# Fritzing sketch connection_scheme (saved by Fritzing 0.9.5d)
perfboards: 1

parts:
  8_4V_->_5V = LM2596 step down module
  Компонент2 = TE466 [part_number=TE466]
  Steering_control = Basic Servo
  Wheels = DC Motor
  Battery_1 = battery_holder_single_18650
  Battery_2 = battery_holder_single_18650
  Type-c_2s_BMS_Charger = 2S-BMS
  U1 = OV7670 Camera [package=camera_sfv24r-2st_2]
  MH-ET_LIVE_ESP32_DEVKIT1 = MH-ET LIVE ESP32 DEVKIT 38 pins
  R1 = Resistor [tolerance=±5% resistance=5100 package=THT]
  R2 = Resistor [tolerance=±5% resistance=5100 package=THT]
  Side_sensor = hc_sro4
  Forward_sensor = hc_sro4

nets:
  N1: 8_4V_->_5V.IN+, Компонент2.Pin_11, Battery_1.+#0, Type-c_2s_BMS_Charger.pin1
  GND: 8_4V_->_5V.IN-, 8_4V_->_5V.OUT-, Компонент2.Pin_2, Компонент2.Pin_8, Steering_control.gnd, Battery_2.+#1, Type-c_2s_BMS_Charger.pin2, U1.GND, MH-ET_LIVE_ESP32_DEVKIT1.GND#64, Side_sensor.GND, Forward_sensor.GND
  VCC: 8_4V_->_5V.OUT+, Компонент2.Pin_1, Steering_control.vcc, MH-ET_LIVE_ESP32_DEVKIT1.5V, Side_sensor.VCC, Forward_sensor.VCC
  N2: Компонент2.Pin_5, MH-ET_LIVE_ESP32_DEVKIT1.IO5
  N3: Компонент2.Pin_6, MH-ET_LIVE_ESP32_DEVKIT1.IO26
  N4: Компонент2.Pin_7, MH-ET_LIVE_ESP32_DEVKIT1.IO25
  N5: Компонент2.Pin_9, Wheels.pin_2
  N6: Компонент2.Pin_10, Wheels.pin_1
  N7: Steering_control.pulse, MH-ET_LIVE_ESP32_DEVKIT1.IO23
  N8: Battery_1.+#1, Battery_2.+#0, Type-c_2s_BMS_Charger.pin3
  3V3: U1.3V3, MH-ET_LIVE_ESP32_DEVKIT1.3V3, R1.Pin_0, R2.Pin_0
  N9: U1.SIOC, MH-ET_LIVE_ESP32_DEVKIT1.IO22, R2.Pin_1
  N10: U1.VSYNC, MH-ET_LIVE_ESP32_DEVKIT1.IO34
  N11: U1.PCLK, MH-ET_LIVE_ESP32_DEVKIT1.IO33
  N12: U1.D7, MH-ET_LIVE_ESP32_DEVKIT1.IO4
  N13: U1.D5, MH-ET_LIVE_ESP32_DEVKIT1.IO13
  N14: U1.D3, MH-ET_LIVE_ESP32_DEVKIT1.IO15
  N15: U1.D1, MH-ET_LIVE_ESP32_DEVKIT1.IO17
  N16: U1.SIDO, MH-ET_LIVE_ESP32_DEVKIT1.IO21, R1.Pin_1
  N17: U1.HREF, MH-ET_LIVE_ESP32_DEVKIT1.IO35
  N18: U1.XCLK, MH-ET_LIVE_ESP32_DEVKIT1.IO32
  N19: U1.D6, MH-ET_LIVE_ESP32_DEVKIT1.IO12
  N20: U1.D4, MH-ET_LIVE_ESP32_DEVKIT1.IO14
  N21: U1.D2, MH-ET_LIVE_ESP32_DEVKIT1.IO16
  N22: U1.D0, MH-ET_LIVE_ESP32_DEVKIT1.IO27
  N23: MH-ET_LIVE_ESP32_DEVKIT1.SVP, Side_sensor.Echo
  N24: MH-ET_LIVE_ESP32_DEVKIT1.IO19, Forward_sensor.Trig
  N25: MH-ET_LIVE_ESP32_DEVKIT1.IO18, Forward_sensor.Echo
  N26: MH-ET_LIVE_ESP32_DEVKIT1.IO2, Side_sensor.Trig

custom parts:
  LM2596 step down module: LM2596 DC-DC step down power supply module 3 A.
  TE466: Description: This is essentially a ramped up version of our Ardumoto motor driver shield. For this monster shield we've replaced the L298 H-bridge with a pair of VNH2SP30 full-bridge motor drivers. We've also beefed up the support circuitry so this board is capable of driving a pair of high-current motors! The VIN and motor out are pitched for our 5mm screw terminals (not included), making it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
  battery_holder_single_18650: single 18650 battery holder
  2S-BMS: 2S-BMS LIPO battery charger / protection unit. Note pcb does not match the board as it will likely connect with wires, so pcb is 5 pads suitable for .1in header pins.
  OV7670 Camera: CMOS image sensor
  MH-ET LIVE ESP32 DEVKIT 38 pins: http://mh.nodebb.com/topic/2/mh-et-live-esp32-devkit

// code stored in the sketch: washer.ino

